// Logisim project scheme.circ as structural Verilog: 1 circuit, main circuit main
module main (
  input  x2,
  input  x1,
  input  x0,
  output y1,
  output y0
);

  wire and_1_out, and_2_out, and_3_out, not_1_out, not_2_out, not_3_out, Q0_q, Q0_qn, Q1_q, Q1_qn, Q2_q,
       Q2_qn;

  not not_1 (not_1_out, x2);
  not not_2 (not_2_out, x1);
  not not_3 (not_3_out, x0);
  and and_1 (and_1_out, not_1_out, Q1_q);
  // AND_Gate and_2 has open pins: out=and_2_out
  // AND_Gate and_3 has open pins: out=and_3_out
  // OR_Gate or_1 has open pins: in0=and_1_out, in1=and_2_out, out=open
  S_R_Flip_Flop Q2 (.Q(Q2_q), .Qn(Q2_qn));  // open: S, clk, R, preset, reset, en
  D_Flip_Flop Q1 (.Q(Q1_q), .Qn(Q1_qn));  // open: clk, D, preset, en, reset
  T_Flip_Flop Q0 (.Q(Q0_q), .Qn(Q0_qn));  // open: clk, T, preset, reset, en
endmodule
